// Logisim project hbcpu.circ as structural Verilog
module LeftShift (
  input  [7:0] A,
  input  [7:0] B,
  output [7:0] O,
  output COut
);

  wire and_1_out, and_2_out, and_3_out, and_4_out, or_1_out, or_2_out, or_3_out, or_4_out;
  wire [7:0] multiplexer_1_out, multiplexer_2_out, multiplexer_3_out;

  or or_1 (or_1_out, A[4], A[5], A[6], A[7]);
  Multiplexer #(.width(8)) multiplexer_1 (.in0(A), .in1({A[3:0], 4'b0000}), .out(multiplexer_1_out), .sel(B[2]));
  and and_1 (and_1_out, or_1_out, B[2]);
  or or_2 (or_2_out, multiplexer_1_out[6], multiplexer_1_out[7]);
  Multiplexer #(.width(8)) multiplexer_2 (
    .in0(multiplexer_1_out), .in1({multiplexer_1_out[5:0], 2'b00}), .out(multiplexer_2_out), .sel(B[1]));
  and and_2 (and_2_out, or_2_out, B[1]);
  Multiplexer #(.width(8)) multiplexer_3 (
    .in0(multiplexer_2_out), .in1({multiplexer_2_out[6:0], 1'b0}), .out(multiplexer_3_out), .sel(B[0]));
  and and_3 (and_3_out, multiplexer_2_out[7], B[0]);
  or or_3 (or_3_out, B[7], B[6], B[5], B[4], B[3]);
  or or_4 (or_4_out, A[0], A[1], A[2], A[3], A[4], A[5], A[6], A[7]);
  Multiplexer #(.width(8)) multiplexer_4 (.in0(multiplexer_3_out), .in1({8{1'b0}}), .out(O), .sel(or_3_out));
  and and_4 (and_4_out, or_3_out, or_4_out);
  or or_5 (COut, and_3_out, and_2_out, and_1_out, and_4_out);

  // Notes on the sheet:
  //   Left Shift
endmodule

module RightShift (
  input  [7:0] A,
  input  [7:0] B,
  input  ARITH,
  output [7:0] O,
  output COut
);

  wire and_2_out, and_3_out, and_4_out, and_5_out, or_1_out, or_2_out, or_3_out, or_4_out;
  wire [7:0] multiplexer_1_out, multiplexer_2_out, multiplexer_3_out;
  wire [7:7] and_1_out;

  or or_1 (or_1_out, A[0], A[1], A[2], A[3]);
  and and_1 (and_1_out[7], A[7], ARITH);
  Multiplexer #(.width(8)) multiplexer_1 (
    .in0(A), .in1({{4{and_1_out[7]}}, A[7:4]}), .out(multiplexer_1_out), .sel(B[2]));
  and and_2 (and_2_out, or_1_out, B[2]);
  or or_2 (or_2_out, multiplexer_1_out[0], multiplexer_1_out[1]);
  Multiplexer #(.width(8)) multiplexer_2 (
    .in0(multiplexer_1_out), .in1({{2{and_1_out[7]}}, multiplexer_1_out[7:2]}), .out(multiplexer_2_out),
    .sel(B[1]));
  and and_3 (and_3_out, or_2_out, B[1]);
  Multiplexer #(.width(8)) multiplexer_3 (
    .in0(multiplexer_2_out), .in1({and_1_out[7], multiplexer_2_out[7:1]}), .out(multiplexer_3_out), .sel(B[0]));
  and and_4 (and_4_out, multiplexer_2_out[0], B[0]);
  or or_3 (or_3_out, B[7], B[6], B[5], B[4], B[3]);
  or or_4 (or_4_out, A[0], A[1], A[2], A[3], A[4], A[5], A[6], A[7]);
  Multiplexer #(.width(8)) multiplexer_4 (.in0(multiplexer_3_out), .in1({8{and_1_out[7]}}), .out(O), .sel(or_3_out));
  and and_5 (and_5_out, or_3_out, or_4_out);
  or or_5 (COut, and_4_out, and_3_out, and_2_out, and_5_out);

  // Notes on the sheet:
  //   Right Shift
endmodule

module ALU (
  input  [7:0] A,
  input  [7:0] B,
  input  CIn,
  input  [3:0] OP,
  output [7:0] O,
  output COut
);

  wire aluadder_1_cout, leftshift_1_cout, rightshift_1_cout;
  wire [7:0] aluadder_1_o, alulogic_1_o, leftshift_1_o, rightshift_1_o;

  // NoConnect on OP[1]
  LeftShift leftshift_1 (.A(A), .B(B), .O(leftshift_1_o), .COut(leftshift_1_cout));
  RightShift rightshift_1 (.A(A), .B(B), .ARITH(OP[0]), .O(rightshift_1_o), .COut(rightshift_1_cout));
  AluAdder aluadder_1 (.CIn(CIn), .OP(OP[1:0]), .A(A), .B(B), .O(aluadder_1_o), .COut(aluadder_1_cout));
  AluLogic alulogic_1 (.A(A), .B(B), .OP(OP[1:0]), .O(alulogic_1_o));
  Multiplexer #(.select(2), .width(8)) multiplexer_1 (
    .in0(leftshift_1_o), .in1(rightshift_1_o), .in2(aluadder_1_o), .in3(alulogic_1_o), .out(O));  // open: sel
  Multiplexer #(.select(2)) multiplexer_2 (
    .in0(leftshift_1_cout), .in1(rightshift_1_cout), .in2(aluadder_1_cout), .in3(1'b0), .out(COut));  // open: sel
endmodule

module Adder8Bit (
  input  CIn,
  input  [7:0] A,
  input  [7:0] B,
  output [7:0] O,
  output COut
);

  wire adder1bit_1_cout, adder1bit_2_cout, adder1bit_3_cout, adder1bit_4_cout, adder1bit_5_cout,
       adder1bit_6_cout, adder1bit_7_cout;

  Adder1Bit adder1bit_1 (.A(A[0]), .B(B[0]), .CIn(CIn), .O(O[0]), .COut(adder1bit_1_cout));
  Adder1Bit adder1bit_2 (.A(A[1]), .B(B[1]), .CIn(adder1bit_1_cout), .O(O[1]), .COut(adder1bit_2_cout));
  Adder1Bit adder1bit_3 (.A(A[2]), .B(B[2]), .CIn(adder1bit_2_cout), .O(O[2]), .COut(adder1bit_3_cout));
  Adder1Bit adder1bit_4 (.A(A[3]), .B(B[3]), .CIn(adder1bit_3_cout), .O(O[3]), .COut(adder1bit_4_cout));
  Adder1Bit adder1bit_5 (.A(A[4]), .B(B[4]), .CIn(adder1bit_4_cout), .O(O[4]), .COut(adder1bit_5_cout));
  Adder1Bit adder1bit_6 (.A(A[5]), .B(B[5]), .CIn(adder1bit_5_cout), .O(O[5]), .COut(adder1bit_6_cout));
  Adder1Bit adder1bit_7 (.A(A[6]), .B(B[6]), .CIn(adder1bit_6_cout), .O(O[6]), .COut(adder1bit_7_cout));
  Adder1Bit adder1bit_8 (.A(A[7]), .B(B[7]), .CIn(adder1bit_7_cout), .O(O[7]), .COut(COut));
endmodule

module Adder1Bit (
  input  A,
  input  B,
  input  CIn,
  output O,
  output COut
);

  wire and_1_out, and_2_out, xor_1_out;

  xor xor_1 (xor_1_out, A, B);
  and and_1 (and_1_out, A, B);
  xor xor_2 (O, xor_1_out, CIn);
  and and_2 (and_2_out, xor_1_out, CIn);
  or or_1 (COut, and_1_out, and_2_out);
endmodule

module AluLogic (
  input  [7:0] A,
  input  [7:0] B,
  input  [1:0] OP,
  output [7:0] O
);

  wire [7:0] and_1_out, not_1_out, or_1_out, xor_1_out;

  assign and_1_out = A & B;  // AND_Gate and_1, 8 bits wide
  assign or_1_out = A | B;  // OR_Gate or_1, 8 bits wide
  assign xor_1_out = A ^ B;  // XOR_Gate xor_1, 8 bits wide
  assign not_1_out = ~A;  // NOT_Gate not_1, 8 bits wide
  Multiplexer #(.select(2), .width(8)) multiplexer_1 (
    .in0(and_1_out), .in1(or_1_out), .in2(xor_1_out), .in3(not_1_out), .out(O), .sel(OP));
endmodule

module AluAdder (
  input  CIn,
  input  [1:0] OP,
  input  [7:0] A,
  input  [7:0] B,
  output [7:0] O,
  output COut
);

  wire multiplexer_1_out, pull_resistor_1_node, pull_resistor_2_node;
  wire [7:0] multiplexer_2_out, not_1_out;

  Pull_Resistor #(.pull(1)) pull_resistor_1 (.node(pull_resistor_1_node));
  Pull_Resistor pull_resistor_2 (.node(pull_resistor_2_node));
  Multiplexer #(.select(2)) multiplexer_1 (
    .in0(pull_resistor_2_node), .in1(pull_resistor_1_node), .in2(CIn), .in3(CIn), .out(multiplexer_1_out),
    .sel(OP));
  assign not_1_out = ~B;  // NOT_Gate not_1, 8 bits wide
  // NoConnect on OP[1]
  Multiplexer #(.width(8)) multiplexer_2 (.in0(B), .in1(not_1_out), .out(multiplexer_2_out), .sel(OP[0]));
  Adder8Bit adder8bit_1 (.CIn(multiplexer_1_out), .A(A), .B(multiplexer_2_out), .O(O), .COut(COut));

  // Notes on the sheet:
  //   00 ADD
  //   01 SUB
  //   10 ADDC
  //   11 SUBB
endmodule
